# Fritzing sketch turnout array (saved by Fritzing 0.9.9b)

parts:
  PWM_Driver = 16-Channel 12-bit PWM Servo Driver - I2C [part_number=815]
  Microprocessor = Adafruit Metro Mini [part_number="Adafruit #2590"]
  C1 = Capacitor Polarized [package=cpol-radial-1000uf-25v]
  J7 = Basic Servo
  J6 = Basic Servo
  J5 = Basic Servo
  J4 = Basic Servo
  J3 = Basic Servo
  J2 = Basic Servo
  J1 = Basic Servo
  J0 = Basic Servo
  V1 = DC Power [voltage=5]

nets:
  VCC: PWM_Driver.5.0V, Microprocessor.VIN, C1.+, J7.vcc, J6.vcc, J5.vcc, J4.vcc, J3.vcc, J2.vcc, J1.vcc, J0.vcc, V1.V+
  GND: PWM_Driver.GND, Microprocessor.GND, C1.-, J7.gnd, J6.gnd, J5.gnd, J4.gnd, J3.gnd, J2.gnd, J1.gnd, J0.gnd, V1.V-
  N1: PWM_Driver.PWM7, J7.pulse
  N2: PWM_Driver.PWM6, J6.pulse
  N3: PWM_Driver.PWM5, J5.pulse
  N4: PWM_Driver.PWM4, J4.pulse
  N5: PWM_Driver.PWM3, J3.pulse
  N6: PWM_Driver.PWM2, J2.pulse
  N7: PWM_Driver.PWM1, J1.pulse
  N8: PWM_Driver.PWM0, J0.pulse
  VCC_2: PWM_Driver.VCC, Microprocessor.+5V
  N9: PWM_Driver.SDA, Microprocessor.AD4/SDA
  N10: PWM_Driver.SCL, Microprocessor.AD5/SCL

custom parts:
  16-Channel 12-bit PWM Servo Driver - I2C: You want to make a cool robot, maybe a hexapod walker, or maybe just a piece of art with a lot of moving parts. Or maybe you want to drive a lot of LEDs with precise PWM output. Using only two pins, control 16 free-running PWM outputs! You can even chain up 62 breakouts to control up to 992 PWM outputs.
  Adafruit Metro Mini: We sure love the ATmega328 here at Adafruit, and we use them a lot for our own projects. The processor has plenty of GPIO, Analog inputs, hardware UART SPI and I2C, timers and PWM galore - just enough for most simple projects. When we need to go small, we use a Pro Trinket 3V or 5V, but if you want to have USB-to-Serial built in, we reach for an Adafruit METRO Mini. METRO Mini is the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

// code stored in the sketch: turnout_servo_sketchbook.ino
 
/*
 * This program is based on example code for the
 * Adafruit 16-channel PWM & servo driver
 * written by Limor Fried/Ladyada for Adafruit Industries.
 * 
 * Other ideas and code from:
 *  http://www.motorhomesites.org.uk/railway/JMRI_Arduino_Setup.php
 *  https://www.jmri.org/help/en/html/hardware/arduino/index.shtml
 *  
 *  The program will control up to eight servos using the
 *  writeMicroseconds command for PWM control.
 *  
 *  Slow motion is obtained by incrementing the PWM command.
 *  
 *  Equipment needed:
 *    Microcontroller - for this version I used an Arduino Uno Rev3
 *    Adafruit PCA9685 PMW servo driver
 *    Generic RC airplane type servos
 *    Generic toggle switches
 *    DCC System (I use an NCE PowerCab)
 *    JMRI server (I use JMRI on a Raspberry Pi)
 *    USB communications between JMRI server and Microcontroller.
 */

#include <CMRI.h> //  Arduino C/MRI library https://github.com/madleech/ArduinoCMRI
#include <Auto485.h> // Automatic RS485 Wrapper library https://github.com/madleech/Auto485
#include <Adafruit_PWMServoDriver.h> // Adafruit PWM servo driver library
      // https://github.com/adafruit/Adafruit-PWM-Servo-Driver-Library

//  Adafruit_PWMServoDriver pwm0 = Adafruit_PWMServoDriver(0x40);
Adafruit_PWMServoDriver pwm1 = Adafruit_PWMServoDriver(0x41); //testing adafruit board 1
//  Adafruit_PWMServoDriver pwm2 = Adafruit_PWMServoDriver(0x42);

#define CMRI_ADD1 1 //  sets CMRI address for the first device
#define DE_PIN 2 //  somthing to do with RS-485

//  setup a CMRI device
CMRI cmri(CMRI_ADD1,24,48); // defaults to an SMINI 0,24,48

/*  servo travel limits - these will need to be set up for the individual servos
 *  USMIN is minimum travel, USST is starting poing, and USMAX is maximum travel */

const int USLIM[3][8] = {
  {1200,1200,1200,1000,1000,1000,1000,1000},
  {1200,1200,1200,1000,1000,1000,1000,1000},
  {1600,1600,1600,1800,1800,1800,1800,1800},
};

Auto485 bus(DE_PIN); // arduino pin 2 for DE and RE pins

const int SERVO_FREQ = 60;  // Try 50 Hz if 60 does not work

//  time delays
unsigned long ztime = 0;
const long tdel1 = 5; // time delay 1 (ms)

/*  
 *  Turnout inputs:
 *  These are the digital addresses (CMRI-1) for the turnouts.
 *  Since there are eight turnouts we will use 40-47 to
 *  represent eight CMRI addresses from 41 to 48.
 */
const int turnOut[] = {40,41,42,43,44,45,46,47};

/*  servo position variable in microseconds (approximate but seems to be consistent)
 *  servos are numbered from 0 to 15. */
 
int psec[8];
int swstate[8];

void moveTurnout(byte x,int y) {

    if (y==1) {
      if (psec[x] < USLIM[2][x]) {
        psec[x] = psec[x] + 5;
        pwm1.writeMicroseconds(x, psec[x]);
      }
    }
  
    else {
      if (psec[x] > USLIM[0][x]) {
        psec[x] = psec[x] - 5;
        pwm1.writeMicroseconds(x, psec[x]);
      }
    }
}

void setup() {
 
/*  these 3 lines set up the PWM driver. They must be run for every board.
 *  the following commands set up the PWM boards' operating frequencies.
 *  this is necessary for consistent servo positions. */
 
  pwm1.begin(); //the 0x40 board is "pwm0"
    //t
    //this is necessary for consistent servo positions.
    pwm1.setOscillatorFrequency(27000000);
    pwm1.setPWMFreq(SERVO_FREQ);

  //  this starts the RS485 bus defined above
  bus.begin(9600);

  //input the initial position variables in usec
  
    for (byte i = 0; i <8; i++) {
      psec[i] = USLIM[1][i];
    }
 
    for (byte i = 0; i <8; i++) {
      moveTurnout(i,swstate[i]);
    }
  }

void loop() {

//  main processing node of cmri library
  cmri.process();

 // we are not in any hurry
 unsigned long otime = millis();

  if (otime - ztime >= tdel1) {

    // save the last time you blinked the LED
    
    ztime = otime;


/*  this for statement reads CMRI and sets the swstate[i] according to
 *  the pin state. This section can be elaborated to add interlocks or
 *  other automation. */
  
    for (byte i = 0; i <8; i++) {
      swstate[i] = cmri.get_bit(turnOut[i]);
    }

/*
 *  this statement calls the movement function
 *  for every turnout based on its swstate[]
 */
  
    for (byte i = 0; i <8; i++) {
        moveTurnout(i,swstate[i]);
    }
  }
}

// code stored in the sketch: turnoutservo_array.ino

/***************************************
  This code is based on the example for the Adafruit 16-channel PWM & servo driver
  written by Limor Fried/Ladyada for Adafruit Industries.

	The code supports the Arduino Uno R3. I am using an Adafruit Metro Mini as
	the microcontroller and it works OK except pin 13 does not work for this
	application.

  This sketch uses arrays to address pins and servos
  and to set servo limits.
  
  This sketch has no feedback from the servos or other inputs.

  I use 10 servos in this sketch because the layout I am planning has ten.
  
  The hardware is cheap so there is no reason not to have
  a separate microcontroller for every 10 turnouts.
 ***************************************/

#include <Wire.h> //these are Arduino libraries with special commands 
#include <Adafruit_PWMServoDriver.h> //this is the library specific to the PWM driver

Adafruit_PWMServoDriver pwm0 = Adafruit_PWMServoDriver(0x40); //this names the board with address 0x40 "pwm0"
// 0x40 is the default address so it can be represented as "()"
// Adafruit_PWMServoDriver pwm1 = Adafruit_PWMServoDriver(0x41); // Syntax for adding more servo drivers

// servo travel limits - these will need to be set up for the individual servos
const int USMIN[10] = {1000,1000,1000,1000,1000,1000,1000,1000,1000,1000}; // minimum servo travel
const int USCEN[10] = {1400,1400,1400,1400,1400,1400,1400,1400,1400,1400}; // neutral point
const int USMAX[10] = {1800,1800,1400,1400,1400,1400,1400,1400,1400,1400}; // maximum servo travel

// servo frequency. This will be used in the setup loop.
const int SERVO_FREQ = 60;  // Try 50 Hz if 60 does not work.

/*  Digital input pins
 *  pinX is for input pin Y
 *  This array reserves pins 0 and 1 for serial communications
 *  and two of the six pins that can be used for PWM output (3 and 6) */ 
const uint8_t pinNum[10] = {2,4,5,7,8,9,10,11,12,13};

// servo position in microseconds (approximate but seems to be consistent)
// servos are numbered from 0 to 15
int psec[10]; // psec[#] is postion in usec for servo #
int tpos; // this is the temporary position

void setup() {
   Serial.begin(9600); //sets up the serial output for the Arduino for debugging
  Serial.println("Program Running");

    //set up the pins
    for (byte i = 0; i <10; i = i +1) {
      pinMode(pinNum[i], INPUT_PULLUP);
          }
  // sets up the PWM driver. Run these 3 lines for each board.
  pwm0.begin(); //the 0x40 board is "pwm0"
    //the following commands set up the PWM boards' operating frequencies.
    //this is necessary for consistent servo positions.
     pwm0.setOscillatorFrequency(27000000);
     pwm0.setPWMFreq(SERVO_FREQ);
}

void loop() {

  for (byte i = 0; i <10; i = i +1) {
    
    if (digitalRead(pinNum[i])==HIGH) {
      if (psec[i] < USMAX[i]) {
      psec[i]++;
      pwm0.writeMicroseconds(i, psec[i]);
     }
    }

    if (digitalRead(pinNum[i])==LOW) {
      if (psec[i] < USMIN[i]) {
      psec[i]--;
      pwm0.writeMicroseconds(i, psec[i]);
     }

    }
   }

}
